# Fritzing sketch SimpleRGBController (saved by Fritzing 0.9.4)
breadboards: 1

parts:
  Raspberry_Pi_1 = Raspberry Pi 3 [part_number=RPI-3-V1.2]
  Part1 = 12-Channel 16-bit PWM LED Driver - SPI [part_number=1455]
  Q1 = Basic FET N-Channel [package="DPak [SMD]"]
  Q2 = Basic FET N-Channel [package="DPak [SMD]"]
  Q3 = Basic FET N-Channel [package="DPak [SMD]"]
  RGB_Strip_LED2 = RGB Strip LED
  JACK1 = 2.1mm Barrel Jack with Terminal Block

nets:
  3V3: Raspberry_Pi_1.3v3, Raspberry_Pi_1.GPIO2, Raspberry_Pi_1.GPIO3, Raspberry_Pi_1.3V3, Raspberry_Pi_1.GIPO10, Part1.VCC, Part1.DI, Part1.V+
  GND: Raspberry_Pi_1.GND, Part1.GND, Q1.source, Q2.source, Q3.source, JACK1.NEG
  N1: Raspberry_Pi_1.GIPO9, Raspberry_Pi_1.GIPO11, Raspberry_Pi_1.ID_SD, Part1.CI
  N2: Part1.R0, Q1.Gate
  N3: Part1.G0, Q2.Gate
  N4: Part1.B0, Q3.Gate
  N5: Q1.drain, RGB_Strip_LED2.Red_Connect#6
  N6: Q2.drain, RGB_Strip_LED2.Green_Connect#7
  N7: Q3.drain, RGB_Strip_LED2.Blue_Connect#5
  N8: RGB_Strip_LED2.Common_Connect#4, JACK1.POS

custom parts:
  12-Channel 16-bit PWM LED Driver - SPI: This chip can control 12 separate channels of 16-bit PWM output. This is the highest-resolution PWM board we've seen! Designed (and ideal) for precision LED control, this board is NOT good for driving servos. Only two "SPI" pins are required to send data, and the design is completely chainable. As long as there's enough power for all the boards you can chain as many as you'd like.
  RGB Strip LED: A tri-color Strip LED with red, green and blue. Pin order: red - common cathode - blue - green
